// Logisim project Group5_PartA.circ as structural Verilog
module Reg16bit (
  input  [15:0] in_1,
  input  in_2,
  input  in_3,
  output [15:0] out_4
);

  Register #(.width(16)) register_1 (.D(in_1), .en(in_3), .clk(in_2), .Q(out_4));  // open: clr
endmodule
